// Digital circuit 3bit_PROGRAM_COUNTER.dig as structural Verilog
module _3bit_PROGRAM_COUNTER (
  input  [2:0] I_2_0,
  input  CLK,
  output [2:0] O_2_0
);

  _1bit_Register _1bit_register_1 (.Dout(O_2_0[2]), .Din(I_2_0[2]), .Sel(1'b1), .CLK(CLK));
  _1bit_Register _1bit_register_2 (.Dout(O_2_0[1]), .Din(I_2_0[1]), .Sel(1'b1), .CLK(CLK));
  _1bit_Register _1bit_register_3 (.Dout(O_2_0[0]), .Din(I_2_0[0]), .Sel(1'b1), .CLK(CLK));

  // Other names for the same wires on the sheet: Dout0 = O_2_0[0]; Dout1 = O_2_0[1]; Dout2 = O_2_0[2];
  //   Din0 = I_2_0[0]; Din1 = I_2_0[1]; Din2 = I_2_0[2]
endmodule
