// Digital circuit 4_bit_adder.dig as structural Verilog
module _4_bit_adder (
  input  [3:0] A_3_0,
  input  [3:0] B_3_0,
  output [3:0] R_3_0,
  output Cout
);

  wire fa_2_cout, fa_3_cout, fa_4_cout;

  FA fa_1 (.Cin(fa_2_cout), .S(R_3_0[3]), .Cout(Cout), .X(A_3_0[3]), .Y(B_3_0[3]));
  FA fa_2 (.Cin(fa_3_cout), .S(R_3_0[2]), .Cout(fa_2_cout), .X(A_3_0[2]), .Y(B_3_0[2]));
  FA fa_3 (.Cin(fa_4_cout), .S(R_3_0[1]), .Cout(fa_3_cout), .X(A_3_0[1]), .Y(B_3_0[1]));
  FA fa_4 (.Cin(1'b0), .S(R_3_0[0]), .Cout(fa_4_cout), .X(A_3_0[0]), .Y(B_3_0[0]));
endmodule
