// Digital circuit 4bit REG SET.dig as structural Verilog
module _4bit_REG_SET (
  input  [3:0] WRD_3_0,
  input  [1:0] WR_1_0,
  input  WE,
  input  [1:0] RA_1_0,
  input  [1:0] RB_1_0,
  input  CLK,
  output [3:0] A_3_0,
  output [3:0] B_3_0
);

  wire A0, A1, A2, D0, D1, D2, decoder_1_out_3;
  wire [3:0] R0, R1, R2;

  and and_1 (D2, A2, WE);
  Decoder #(.Selector_Bits(2)) decoder_1 (.sel(WR_1_0), .out_0(A0), .out_1(A1), .out_2(A2), .out_3(decoder_1_out_3));
  and and_2 (D0, A0, WE);
  and and_3 (D1, A1, WE);
  _4bit_REGISTER _4bit_register_1 (.Dout_3_0(R2), .Din_3_0(WRD_3_0), .Sel(D2), .CLK(CLK));
  _4bit_REGISTER _4bit_register_2 (.Dout_3_0(R1), .Din_3_0(WRD_3_0), .Sel(D1), .CLK(CLK));
  _4bit_REGISTER _4bit_register_3 (.Dout_3_0(R0), .Din_3_0(WRD_3_0), .Sel(D0), .CLK(CLK));
  Multiplexer #(.Selector_Bits(2), .Bits(4)) multiplexer_1 (
    .sel(RA_1_0), .in_0(R0), .in_1(R1), .in_2(R2), .in_3(4'b0000), .out(A_3_0));
  Multiplexer #(.Selector_Bits(2), .Bits(4)) multiplexer_2 (
    .sel(RB_1_0), .in_0(R0), .in_1(R1), .in_2(R2), .in_3(4'b0000), .out(B_3_0));
  // also tied to GND on the sheet: decoder_1_out_3
endmodule
