// Digital circuit 4bit_ALU.dig as structural Verilog
module _4bit_ALU (
  input  [3:0] A_3_0,
  input  [3:0] B_3_0,
  input  [1:0] OP_1_0,
  output [3:0] R_3_0
);

  wire [3:0] _4_bit_adder_1_r_3_0, _4bit_not_1_r_3_0, _4bit_shr_1_r_3_0;

  _4_bit_adder _4_bit_adder_1 (.A_3_0(A_3_0), .B_3_0(B_3_0), .R_3_0(_4_bit_adder_1_r_3_0));  // open: Cout
  _4bit_SHR _4bit_shr_1 (.A_3_0(A_3_0), .Sel_1_0(B_3_0[1:0]), .R_3_0(_4bit_shr_1_r_3_0));
  _4bit_NOT _4bit_not_1 (.A_3_0(A_3_0), .R_3_0(_4bit_not_1_r_3_0));
  Multiplexer #(.Selector_Bits(2), .Bits(4)) multiplexer_1 (
    .sel(OP_1_0), .in_0(_4_bit_adder_1_r_3_0), .in_1(_4bit_shr_1_r_3_0), .in_2(_4bit_not_1_r_3_0),
    .in_3(4'b0000), .out(R_3_0));

  // Other names for the same wires on the sheet: A[3:0] = A_3_0; B[3:0] = B_3_0
endmodule
