// Digital circuit 4bit_CPU.dig as structural Verilog
module _4bit_CPU (
  input  [2:0] WR_2_0,
  input  [14:0] WRD_14_0,
  input  WE,
  input  CLK,
  input  PC_EN,
  input  [2:0] RA2_2_0,
  input  ZF,
  input  SF,
  output [14:0] RD2_14_0,
  output [1:0] R1_1_0,
  output [1:0] R2__1_0,
  output [1:0] WR_1_0,
  output [3:0] R_3_0,
  output [3:0] A_3_0,
  output [3:0] B_3_0,
  output [2:0] JMP_ADDR_2_0
);

  wire CPU_CLK, IMM_SEL, JMP_SEL, REG_EN;
  wire [1:0] Op;
  wire [2:0] _3bit_pc_adder_1_o_2_0, _3bit_program_counter_1_o_2_0, multiplexer_1_out;
  wire [3:0] _4bit_reg_set_1_b_3_0;
  wire [6:0] XX;
  wire [14:11] _8x15_ram_1_rd1_14_0;

  Multiplexer #(.Bits(3)) multiplexer_1 (
    .sel(JMP_SEL), .in_0(_3bit_pc_adder_1_o_2_0), .in_1(JMP_ADDR_2_0), .out(multiplexer_1_out));
  _3bit_PC_ADDER _3bit_pc_adder_1 (.I_2_0(_3bit_program_counter_1_o_2_0), .O_2_0(_3bit_pc_adder_1_o_2_0));
  _3bit_PROGRAM_COUNTER _3bit_program_counter_1 (
    .I_2_0(multiplexer_1_out), .CLK(CPU_CLK), .O_2_0(_3bit_program_counter_1_o_2_0));
  and and_1 (CPU_CLK, CLK, PC_EN);
  _8x15_RAM _8x15_ram_1 (
    .RA1_2_0(_3bit_program_counter_1_o_2_0), .RA2_2_0(RA2_2_0), .WR_2_0(WR_2_0), .WRD_14_0(WRD_14_0),
    .WE(WE), .CLK(CLK), .RD1_14_0({_8x15_ram_1_rd1_14_0, JMP_ADDR_2_0, R2__1_0[0], XX}), .RD2_14_0(RD2_14_0));
  _4bit_REG_SET _4bit_reg_set_1 (
    .A_3_0(A_3_0), .B_3_0(_4bit_reg_set_1_b_3_0), .WE(REG_EN), .WRD_3_0(R_3_0), .WR_1_0(JMP_ADDR_2_0[2:1]),
    .CLK(CPU_CLK), .RA_1_0(JMP_ADDR_2_0[2:1]), .RB_1_0({JMP_ADDR_2_0[0], R2__1_0[0]}));
  _4bit_CU _4bit_cu_1 (
    .Opcode_3_0(_8x15_ram_1_rd1_14_0), .SF(SF), .ZF(ZF), .Op_1_0(Op), .REG_EN(REG_EN), .Imm_Sel(IMM_SEL),
    .Jmp_Sel(JMP_SEL));
  _4bit_ALU _4bit_alu_1 (.R_3_0(R_3_0), .A_3_0(A_3_0), .B_3_0(B_3_0), .OP_1_0(Op));
  Multiplexer #(.Bits(4)) multiplexer_2 (
    .sel(IMM_SEL), .in_0(_4bit_reg_set_1_b_3_0), .in_1({JMP_ADDR_2_0, R2__1_0[0]}), .out(B_3_0));

  assign R1_1_0 = JMP_ADDR_2_0[2:1];
  assign R2__1_0[1] = JMP_ADDR_2_0[0];
  assign WR_1_0 = JMP_ADDR_2_0[2:1];

  // Other names for the same wires on the sheet: R2[3:0] = {JMP_ADDR_2_0, R2__1_0[0]};
  //   R2_t[1:0] = {JMP_ADDR_2_0[0], R2__1_0[0]}; JMP_ADDR[2:0] = JMP_ADDR_2_0; R1[1:0] = JMP_ADDR_2_0[2:1];
  //   A[3:0] = A_3_0; B[3:0] = B_3_0; R[3:0] = R_3_0; RD2[14:0] = RD2_14_0

  // Notes on the sheet:
  //   Register Mode (Type of Op =00) = 2bit(Type of op)+2bit(ALU op)+2bit(Reg1)+2bit(Reg2)+7bit(don't care)
  //   Immediate Mode (Type of Op=01) = 2bit(Type of Op)+2bit(ALU Op)+2bit(Reg1)+4bit(Imm value)+5bit(don't care)
  //   Jump Mode (Type of Op=10) = 2bit(Type of Op)+2bit(ALU Op)+3 bit(Address)+8bit(don't care)
  //   JMP (Op=00), JGE
  //   Add(Op=00). SHR(Op=01). NOT(Op=10)
  //   JE START -> 100100100000000
  //   START:
  //   JMP TO ADD R1,5 -> 010001010100000
  //   JMP JMP TO -> 100100100000000
  //   NOT = 001001010000000
endmodule
