// Digital circuit 4bit_NOT.dig as structural Verilog
module _4bit_NOT (
  input  [3:0] A_3_0,
  output [3:0] R_3_0
);

  not not_1 (R_3_0[3], A_3_0[3]);
  not not_2 (R_3_0[2], A_3_0[2]);
  not not_3 (R_3_0[1], A_3_0[1]);
  not not_4 (R_3_0[0], A_3_0[0]);

  // Other names for the same wires on the sheet: A0 = A_3_0[0]; A1 = A_3_0[1]; A2 = A_3_0[2]; A3 = A_3_0[3];
  //   R0 = R_3_0[0]; R1 = R_3_0[1]; R2 = R_3_0[2]; R3 = R_3_0[3]
endmodule
