// Digital circuit 4bit_REGISTER.dig as structural Verilog
module _4bit_REGISTER (
  input  [3:0] Din_3_0,
  input  CLK,
  input  Sel,
  output [3:0] Dout_3_0
);

  _1bit_Register _1bit_register_1 (.Dout(Dout_3_0[3]), .Din(Din_3_0[3]), .Sel(Sel), .CLK(CLK));
  _1bit_Register _1bit_register_2 (.Dout(Dout_3_0[2]), .Din(Din_3_0[2]), .Sel(Sel), .CLK(CLK));
  _1bit_Register _1bit_register_3 (.Dout(Dout_3_0[1]), .Din(Din_3_0[1]), .Sel(Sel), .CLK(CLK));
  _1bit_Register _1bit_register_4 (.Dout(Dout_3_0[0]), .Din(Din_3_0[0]), .Sel(Sel), .CLK(CLK));

  // Other names for the same wires on the sheet: B0 = Dout_3_0[0]; B1 = Dout_3_0[1]; B2 = Dout_3_0[2];
  //   B3 = Dout_3_0[3]; A0 = Din_3_0[0]; A1 = Din_3_0[1]; A2 = Din_3_0[2]; A3 = Din_3_0[3]
endmodule
