// Digital circuit 4bit_SHR.dig as structural Verilog
module _4bit_SHR (
  input  [3:0] A_3_0,
  input  [1:0] Sel_1_0,
  output [3:0] R_3_0
);

  Multiplexer #(.Selector_Bits(2)) multiplexer_1 (
    .sel(Sel_1_0), .in_0(A_3_0[3]), .in_1(1'b0), .in_2(1'b0), .in_3(1'b0), .out(R_3_0[3]));
  Multiplexer #(.Selector_Bits(2)) multiplexer_2 (
    .sel(Sel_1_0), .in_0(A_3_0[2]), .in_1(A_3_0[3]), .in_2(1'b0), .in_3(1'b0), .out(R_3_0[2]));
  Multiplexer #(.Selector_Bits(2)) multiplexer_3 (
    .sel(Sel_1_0), .in_0(A_3_0[1]), .in_1(A_3_0[2]), .in_2(A_3_0[3]), .in_3(1'b0), .out(R_3_0[1]));
  Multiplexer #(.Selector_Bits(2)) multiplexer_4 (
    .sel(Sel_1_0), .in_0(A_3_0[0]), .in_1(A_3_0[1]), .in_2(A_3_0[2]), .in_3(A_3_0[3]), .out(R_3_0[0]));

  // Other names for the same wires on the sheet: A0 = A_3_0[0]; A1 = A_3_0[1]; A2 = A_3_0[2]; A3 = A_3_0[3];
  //   R0 = R_3_0[0]; R1 = R_3_0[1]; R2 = R_3_0[2]; R3 = R_3_0[3]; Sel[1:0] = Sel_1_0
endmodule
